# Fritzing sketch M2.3_LED-Dot-Matrix (saved by Fritzing 0.8.7b)
breadboards: 1

parts:
  Intel(R)_Galileo_1 = Intel(R) Galileo
  8x8_LED_Matrix1 = 8x8 LED Matrix 1388ASR

nets:
  N1: Intel(R)_Galileo_1.A2, 8x8_LED_Matrix1.Pin_5
  N2: Intel(R)_Galileo_1.A3, 8x8_LED_Matrix1.Pin_6
  N3: Intel(R)_Galileo_1.A4/SDA, 8x8_LED_Matrix1.Pin_7#7
  N4: Intel(R)_Galileo_1.A5/SCL, 8x8_LED_Matrix1.Pin_8
  N5: Intel(R)_Galileo_1.D8, 8x8_LED_Matrix1.Pin_15
  N6: Intel(R)_Galileo_1.D9_PWM, 8x8_LED_Matrix1.Pin_16
  N7: Intel(R)_Galileo_1.D10_PWM/SS, 8x8_LED_Matrix1.Pin_4
  N8: Intel(R)_Galileo_1.D11_PWM/MOSI, 8x8_LED_Matrix1.Pin_3
  N9: Intel(R)_Galileo_1.D12/MISO, 8x8_LED_Matrix1.Pin_2
  N10: Intel(R)_Galileo_1.D13/SCK, 8x8_LED_Matrix1.Pin_1
  N11: Intel(R)_Galileo_1.D2, 8x8_LED_Matrix1.Pin_9
  N12: Intel(R)_Galileo_1.D3_PWM, 8x8_LED_Matrix1.Pin_7#10
  N13: Intel(R)_Galileo_1.D4, 8x8_LED_Matrix1.Pin_11
  N14: Intel(R)_Galileo_1.D5_PWM, 8x8_LED_Matrix1.Pin_12
  N15: Intel(R)_Galileo_1.D6_PWM, 8x8_LED_Matrix1.Pin_13
  N16: Intel(R)_Galileo_1.D7, 8x8_LED_Matrix1.Pin14

custom parts:
  Intel(R) Galileo: Galileo is a microcontroller board based on the Intel® Quark SoC X1000 Application Processor, a 32-bit Intel Pentium-class system on a chip (datasheet). It’s the first board based on Intel® architecture designed to be hardware and software pin-compatible with Arduino shields designed for the Uno R3. Digital pins 0 to 13 (and the adjacent AREF and GND pins), Analog inputs 0 to 5, the power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
  8x8 LED Matrix 1388ASR: Red Color Common Anode 8x8 LED Matrix
