# Fritzing sketch M2.2_7-Segment_Display_Shifted (saved by Fritzing 0.9.0b)
breadboards: 1

parts:
  Intel(R)_Galileo_1 = Intel(R) Galileo
  7_Segment2 = 7 Segment Display
  R3 = Resistor [tolerance=±5% resistance=330 package=THT]

nets:
  N1: Intel(R)_Galileo_1.D0/RX, 7_Segment2.Segment_C
  N2: Intel(R)_Galileo_1.D1/TX, 7_Segment2.Segment_D
  N3: Intel(R)_Galileo_1.D2, 7_Segment2.Segment_E
  N4: Intel(R)_Galileo_1.D3_PWM, 7_Segment2.Segment_F
  N5: Intel(R)_Galileo_1.D4, 7_Segment2.Segment_G
  N6: Intel(R)_Galileo_1.D5_PWM, 7_Segment2.Segment_A
  N7: Intel(R)_Galileo_1.D6_PWM, 7_Segment2.Segment_B
  N8: 7_Segment2.common_cathode, R3.Pin_1

custom parts:
  Intel(R) Galileo: Galileo is a microcontroller board based on the Intel® Quark SoC X1000 Application Processor, a 32-bit Intel Pentium-class system on a chip (datasheet). It’s the first board based on Intel® architecture designed to be hardware and software pin-compatible with Arduino shields designed for the Uno R3. Digital pins 0 to 13 (and the adjacent AREF and GND pins), Analog inputs 0 to 5, the power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
